# Fritzing sketch HC-SR501-GPIO4 (saved by Fritzing 0.9.3b)

parts:
  Raspberry_Pi_1 = Raspberry Pi 3 [part_number=RPI-3-V1.2]
  Sensore_PIR_HC-SR501 = HC-SR501 Body Sensor Module

nets:
  N1: Raspberry_Pi_1.GIPO4, Sensore_PIR_HC-SR501.OUT
  GND: Raspberry_Pi_1.GND, Sensore_PIR_HC-SR501.GND
  5V: Raspberry_Pi_1.5V, Sensore_PIR_HC-SR501.VCC

notes:
  5V
  GND
  Trigger

custom parts:
  HC-SR501 Body Sensor Module: Pyroelectric Infrared PIR Motion Sensor Detector Module
